// Digital circuit BR.dig as structural Verilog
module BR (
  input  [31:0] res,
  input  [4:0] rd,
  input  [4:0] rs1,
  input  [4:0] rs2,
  input  W_reg,
  output [31:0] src1,
  output [31:0] src2
);

  wire and_1_out, and_2_out, and_3_out, and_4_out, decoder_1_out_0, decoder_1_out_1, decoder_1_out_2,
       decoder_1_out_3, decoder_2_out_0, decoder_2_out_1, decoder_2_out_2, decoder_2_out_3, decoder_3_out_0,
       decoder_3_out_1, decoder_3_out_2, decoder_3_out_3;
  wire [31:0] registre8_1_src1, registre8_1_src2, registre8_2_src1, registre8_2_src2, registre8_3_src1,
       registre8_3_src2, registre8_4_src1, registre8_4_src2;

  Decoder #(.Selector_Bits(2)) decoder_1 (
    .sel(rd[4:3]), .out_0(decoder_1_out_0), .out_1(decoder_1_out_1), .out_2(decoder_1_out_2),
    .out_3(decoder_1_out_3));
  and and_1 (and_1_out, W_reg, decoder_1_out_0);
  and and_2 (and_2_out, W_reg, decoder_1_out_1);
  and and_3 (and_3_out, W_reg, decoder_1_out_2);
  and and_4 (and_4_out, W_reg, decoder_1_out_3);
  registre8 registre8_1 (
    .\reg (res), .W_reg(and_1_out), .rs1(rs1[2:0]), .rs2(rs2[2:0]), .rd(rd[2:0]), .src1(registre8_1_src1),
    .src2(registre8_1_src2));
  registre8 registre8_2 (
    .\reg (res), .W_reg(and_2_out), .rs1(rs1[2:0]), .rs2(rs2[2:0]), .rd(rd[2:0]), .src1(registre8_2_src1),
    .src2(registre8_2_src2));
  registre8 registre8_3 (
    .\reg (res), .W_reg(and_3_out), .rs1(rs1[2:0]), .rs2(rs2[2:0]), .rd(rd[2:0]), .src1(registre8_3_src1),
    .src2(registre8_3_src2));
  registre8 registre8_4 (
    .\reg (res), .W_reg(and_4_out), .rs1(rs1[2:0]), .rs2(rs2[2:0]), .rd(rd[2:0]), .src1(registre8_4_src1),
    .src2(registre8_4_src2));
  assign src1 = decoder_2_out_0 ? registre8_1_src1 : 32'bz;  // Driver driver_1
  Decoder #(.Selector_Bits(2)) decoder_2 (
    .sel(rs1[4:3]), .out_0(decoder_2_out_0), .out_1(decoder_2_out_1), .out_2(decoder_2_out_2),
    .out_3(decoder_2_out_3));
  assign src1 = decoder_2_out_1 ? registre8_2_src1 : 32'bz;  // Driver driver_2
  assign src1 = decoder_2_out_2 ? registre8_3_src1 : 32'bz;  // Driver driver_3
  assign src1 = decoder_2_out_3 ? registre8_4_src1 : 32'bz;  // Driver driver_4
  assign src2 = decoder_3_out_0 ? registre8_1_src2 : 32'bz;  // Driver driver_5
  Decoder #(.Selector_Bits(2)) decoder_3 (
    .sel(rs2[4:3]), .out_0(decoder_3_out_0), .out_1(decoder_3_out_1), .out_2(decoder_3_out_2),
    .out_3(decoder_3_out_3));
  assign src2 = decoder_3_out_1 ? registre8_2_src2 : 32'bz;  // Driver driver_6
  assign src2 = decoder_3_out_2 ? registre8_3_src2 : 32'bz;  // Driver driver_7
  assign src2 = decoder_3_out_3 ? registre8_4_src2 : 32'bz;  // Driver driver_8
endmodule
