// Digital circuit boite.dig as structural Verilog
module boite (
  input  [2:0] fct3,
  input  [31:0] res,
  output p_np
);

  wire not_1_out, not_2_out, or_1_out;

  Multiplexer #(.Selector_Bits(2)) multiplexer_1 (
    .sel({fct3[2], fct3[0]}), .in_0(not_2_out), .in_1(or_1_out), .in_2(res[31]), .in_3(not_1_out), .out(p_np));
  not not_1 (not_1_out, res[31]);
  not not_2 (not_2_out, or_1_out);
  or or_1 (or_1_out, res[0], res[1], res[2], res[3], res[4], res[5], res[6], res[7], res[8], res[9], res[10], res[11], res[12], res[13], res[14], res[15], res[16], res[17], res[18], res[19], res[20], res[21], res[22], res[23], res[24], res[25], res[26], res[27], res[28], res[29], res[30], res[31]);
endmodule
