// Digital circuit circuit_controle.dig as structural Verilog
module circuit_controle (
  input  clock,
  input  [6:0] OPCODE,
  output GATE_PC,
  output W_MAR,
  output MUX_MDR,
  output W_MDR,
  output W_RI,
  output GATE_MDR,
  output W_PC,
  output GATE_RES,
  output W_REG,
  output MUX_S,
  output MUX_SUB,
  output MUX_UAL,
  output OE_RAM,
  output WE_RAM,
  output MUX_JALR,
  output GATE_RS2
);

  wire and_1_out, and_2_out, and_3_out, and_4_out, and_5_out, and_6_out, and_7_out, and_8_out, and_9_out,
       and_10_out, and_11_out, and_12_out, and_13_out, and_14_out, and_15_out, and_16_out, and_17_out,
       and_18_out, and_19_out, and_20_out, and_21_out, and_22_out, and_23_out, and_24_out, and_25_out,
       and_26_out, and_27_out, and_28_out, and_29_out, and_30_out, and_31_out, and_32_out, and_33_out,
       and_34_out, and_35_out, and_36_out, and_37_out, and_38_out, and_39_out, and_40_out, and_41_out,
       and_42_out, and_43_out, and_44_out, and_45_out, and_46_out, and_47_out, and_48_out, and_50_out,
       and_51_out, and_52_out, and_53_out, and_54_out, and_55_out, and_56_out, and_57_out, and_58_out,
       and_59_out, and_60_out, and_61_out, and_62_out, and_64_out, and_65_out, and_66_out, and_67_out,
       and_68_out, or_1_out, or_2_out, or_3_out, or_4_out, or_5_out, or_6_out, or_7_out, or_8_out, or_13_out,
       Q1_q, Q2_q, Q3_q, Q4_q;

  D_FF Q1 (.D(or_8_out), .C(clock), .Q(Q1_q));  // open: nQ
  D_FF Q2 (.D(or_7_out), .C(clock), .Q(Q2_q));  // open: nQ
  D_FF Q3 (.D(or_5_out), .C(clock), .Q(Q3_q));  // open: nQ
  D_FF Q4 (.D(or_2_out), .C(clock), .Q(Q4_q));  // open: nQ
  and and_1 (and_1_out, and_2_out, ~OPCODE[3]);  // And
  and and_2 (and_2_out, ~Q1_q, Q2_q, Q3_q, ~Q4_q);  // And
  and and_3 (and_3_out, and_2_out, OPCODE[3]);
  and and_4 (and_4_out, ~OPCODE[2], ~OPCODE[3], ~OPCODE[4], ~OPCODE[5], ~OPCODE[6]);  // And
  and and_5 (and_5_out, and_4_out, and_6_out);
  and and_6 (and_6_out, ~Q1_q, Q2_q, ~Q3_q, ~Q4_q);  // And
  and and_7 (and_7_out, Q1_q, ~Q2_q, Q3_q, ~Q4_q);  // And
  or or_1 (or_1_out, and_7_out, and_8_out);
  and and_8 (and_8_out, Q1_q, Q2_q, Q3_q, ~Q4_q);  // And
  or or_2 (or_2_out, or_1_out, or_3_out, and_3_out, and_5_out, and_1_out, and_11_out);
  and and_9 (and_9_out, ~Q1_q, ~Q2_q, ~Q3_q, Q4_q);  // And
  or or_3 (or_3_out, and_9_out, and_10_out);
  and and_10 (and_10_out, ~Q1_q, Q2_q, ~Q3_q, Q4_q);  // And
  and and_11 (and_11_out, Q1_q, Q2_q, ~Q3_q, Q4_q);  // And
  and and_12 (and_12_out, ~OPCODE[2], ~OPCODE[3], ~OPCODE[4], OPCODE[5], ~OPCODE[6]);  // And
  and and_13 (and_13_out, and_12_out, and_14_out);
  and and_14 (and_14_out, ~Q1_q, Q2_q, ~Q3_q, ~Q4_q);  // And
  and and_15 (and_15_out, and_14_out, and_16_out);
  and and_16 (and_16_out, ~OPCODE[2], ~OPCODE[3], OPCODE[4], OPCODE[5], ~OPCODE[6]);  // And
  or or_4 (or_4_out, and_15_out, and_13_out, and_17_out);
  and and_17 (and_17_out, and_14_out, and_18_out);
  and and_18 (and_18_out, ~OPCODE[2], ~OPCODE[3], ~OPCODE[4], OPCODE[5], OPCODE[6]);  // And
  or or_5 (or_5_out, or_4_out, and_1_out, or_6_out);
  or or_6 (or_6_out, and_19_out, and_11_out, and_10_out);
  and and_19 (and_19_out, and_14_out, and_20_out);
  and and_20 (and_20_out, OPCODE[2], ~OPCODE[4], OPCODE[5], OPCODE[6]);  // And
  and and_21 (and_21_out, Q1_q, ~Q2_q, ~Q3_q, ~Q4_q);  // And
  and and_22 (and_22_out, ~Q1_q, Q2_q, ~Q3_q, ~Q4_q);  // And
  and and_23 (and_23_out, and_22_out, and_24_out);
  and and_24 (and_24_out, ~OPCODE[2], ~OPCODE[3], OPCODE[4], ~OPCODE[5], ~OPCODE[6]);  // And
  or or_7 (or_7_out, and_21_out, and_23_out, and_25_out, and_1_out, and_27_out, and_29_out, and_30_out);
  and and_25 (and_25_out, and_22_out, and_26_out);
  and and_26 (and_26_out, OPCODE[2], ~OPCODE[4], OPCODE[5], OPCODE[6]);  // And
  and and_27 (and_27_out, and_22_out, and_28_out);
  and and_28 (and_28_out, ~OPCODE[2], ~OPCODE[3], ~OPCODE[4], OPCODE[5], ~OPCODE[6]);  // And
  and and_29 (and_29_out, Q1_q, Q2_q, Q3_q, ~Q4_q);  // And
  and and_30 (and_30_out, ~Q1_q, ~Q2_q, ~Q3_q, Q4_q);  // And
  or or_8 (or_8_out, and_30_out, and_27_out, and_23_out, and_3_out, and_36_out, and_31_out, and_33_out, and_34_out);
  and and_31 (and_31_out, and_22_out, and_32_out);
  and and_32 (and_32_out, ~OPCODE[2], ~OPCODE[3], ~OPCODE[4], OPCODE[5], OPCODE[6]);  // And
  and and_33 (and_33_out, Q1_q, ~Q2_q, Q3_q, ~Q4_q);  // And
  and and_34 (and_34_out, Q1_q, Q2_q, ~Q3_q, Q4_q);  // And
  and and_35 (and_35_out, and_38_out, ~OPCODE[3]);  // And
  and and_36 (and_36_out, ~Q1_q, ~Q2_q, ~Q3_q, ~Q4_q);  // And
  or or_9 (GATE_PC, and_36_out, and_35_out, and_37_out);
  and and_37 (and_37_out, and_38_out, OPCODE[3]);
  and and_38 (and_38_out, ~Q1_q, Q2_q, Q3_q, ~Q4_q);  // And
  and and_39 (and_39_out, Q1_q, Q2_q, Q3_q, ~Q4_q);  // And
  or or_10 (W_MAR, and_39_out, and_36_out, and_40_out);
  and and_40 (and_40_out, ~Q1_q, ~Q2_q, ~Q3_q, Q4_q);  // And
  and and_41 (and_41_out, Q1_q, ~Q2_q, ~Q3_q, ~Q4_q);  // And
  or or_11 (MUX_MDR, and_41_out, and_42_out);
  and and_42 (and_42_out, Q1_q, Q2_q, ~Q3_q, Q4_q);  // And
  and and_43 (and_43_out, ~Q1_q, Q2_q, ~Q3_q, Q4_q);  // And
  or or_12 (W_MDR, and_43_out, and_41_out, and_44_out);
  and and_44 (and_44_out, Q1_q, Q2_q, ~Q3_q, Q4_q);  // And
  and and_45 (and_45_out, ~Q1_q, Q2_q, ~Q3_q, ~Q4_q);  // And
  and and_46 (and_46_out, ~OPCODE[2], ~OPCODE[3], OPCODE[4], ~OPCODE[5], ~OPCODE[6]);  // And
  and and_47 (and_47_out, ~OPCODE[2], ~OPCODE[3], OPCODE[4], OPCODE[5], ~OPCODE[6]);  // And
  and and_48 (and_48_out, ~OPCODE[2], ~OPCODE[3], ~OPCODE[4], OPCODE[5], OPCODE[6]);  // And
  and and_49 (W_RI, and_45_out, or_13_out);
  or or_13 (or_13_out, and_46_out, and_47_out, and_48_out, and_50_out, and_51_out, and_52_out);
  and and_50 (and_50_out, OPCODE[2], ~OPCODE[4], OPCODE[5], OPCODE[6]);  // And
  and and_51 (and_51_out, ~OPCODE[2], ~OPCODE[3], ~OPCODE[4], OPCODE[5], ~OPCODE[6]);  // And
  and and_52 (and_52_out, ~OPCODE[2], ~OPCODE[3], ~OPCODE[4], ~OPCODE[5], ~OPCODE[6]);  // And
  or or_14 (GATE_MDR, W_RI, and_53_out);
  and and_53 (and_53_out, Q1_q, ~Q2_q, Q3_q, Q4_q);  // And
  or or_15 (W_PC, W_RI, and_54_out, and_55_out);
  and and_54 (and_54_out, Q1_q, ~Q2_q, ~Q3_q, Q4_q);  // And
  and and_55 (and_55_out, ~Q1_q, Q2_q, Q3_q, Q4_q);  // And
  and and_56 (and_56_out, Q1_q, Q2_q, ~Q3_q, ~Q4_q);  // And
  and and_57 (and_57_out, ~Q1_q, ~Q2_q, Q3_q, ~Q4_q);  // And
  or or_16 (GATE_RES, and_56_out, and_57_out, and_58_out, and_59_out);
  and and_58 (and_58_out, Q1_q, Q2_q, Q3_q, ~Q4_q);  // And
  and and_59 (and_59_out, ~Q1_q, ~Q2_q, ~Q3_q, Q4_q);  // And
  or or_17 (W_REG, and_56_out, and_57_out, and_35_out, and_60_out, and_62_out);
  and and_60 (and_60_out, OPCODE[3], and_61_out);
  and and_61 (and_61_out, ~Q1_q, Q2_q, Q3_q, ~Q4_q);  // And
  and and_62 (and_62_out, Q1_q, ~Q2_q, Q3_q, Q4_q);  // And
  and and_63 (MUX_SUB, Q1_q, ~Q2_q, Q3_q, ~Q4_q);  // And
  or or_18 (MUX_S, MUX_SUB, and_64_out);
  and and_64 (and_64_out, Q1_q, Q2_q, Q3_q, ~Q4_q);  // And
  and and_65 (and_65_out, Q1_q, Q2_q, ~Q3_q, ~Q4_q);  // And
  or or_19 (MUX_UAL, and_65_out, and_66_out, and_67_out, and_68_out);
  and and_66 (and_66_out, Q1_q, Q2_q, Q3_q, ~Q4_q);  // And
  and and_67 (and_67_out, ~Q1_q, ~Q2_q, ~Q3_q, Q4_q);  // And
  and and_68 (and_68_out, ~Q1_q, Q2_q, Q3_q, Q4_q);  // And
  and and_69 (OE_RAM, ~Q1_q, ~Q2_q, Q3_q, Q4_q);  // And
  and and_70 (MUX_JALR, ~Q1_q, Q2_q, Q3_q, Q4_q);  // And
  and and_71 (GATE_RS2, ~Q1_q, Q2_q, ~Q3_q, Q4_q);  // And

  assign WE_RAM = OE_RAM;
endmodule
