// Digital circuit circuitdecontrolerv32pipeline.dig as structural Verilog
module circuitdecontrolerv32pipeline (
  input  [6:0] opcode,
  input  [2:0] fct_3,
  output MUX_PC,
  output W_REG,
  output MUX_UAL,
  output MUX_SORTIE,
  output MUX_SUB,
  output OE_RAM,
  output RAM_RESULT,
  output WE_RAM,
  output MUX_IMM,
  output MUX_SW
);

  wire and_1_out, and_2_out, and_3_out, and_4_out, and_5_out, and_6_out, and_7_out, and_9_out, and_10_out,
       and_12_out, and_13_out, and_15_out, and_16_out, and_17_out, and_18_out, and_19_out, not_1_out,
       not_2_out, not_3_out, not_4_out, not_5_out, not_6_out, not_7_out, not_8_out, not_9_out, not_10_out,
       not_11_out, not_12_out, not_13_out, not_14_out, not_15_out, not_16_out, not_17_out, not_18_out,
       not_19_out, not_20_out, not_21_out, not_22_out, not_23_out, not_24_out, not_25_out, not_26_out,
       not_27_out, not_28_out, not_29_out, not_30_out, not_31_out, not_32_out, not_33_out, not_34_out,
       not_35_out, not_36_out, not_37_out, or_1_out, or_2_out, or_3_out, or_4_out, or_5_out, or_6_out,
       or_7_out, or_8_out, or_10_out, or_11_out, or_12_out, or_14_out, or_15_out;

  and and_1 (and_1_out, not_1_out, not_2_out, opcode[4], not_3_out, not_4_out, opcode[1], opcode[0]);
  not not_1 (not_1_out, opcode[6]);
  not not_2 (not_2_out, opcode[5]);
  not not_3 (not_3_out, opcode[3]);
  not not_4 (not_4_out, opcode[2]);
  and and_2 (and_2_out, and_1_out, and_3_out);
  not not_5 (not_5_out, fct_3[2]);
  and and_3 (and_3_out, not_5_out, not_6_out, not_7_out);
  not not_6 (not_6_out, fct_3[1]);
  not not_7 (not_7_out, fct_3[0]);
  and and_4 (and_4_out, not_8_out, opcode[5], opcode[4], not_9_out, not_10_out, opcode[1], opcode[0]);
  not not_8 (not_8_out, opcode[6]);
  not not_9 (not_9_out, opcode[3]);
  and and_5 (and_5_out, and_4_out, and_6_out);
  not not_10 (not_10_out, opcode[2]);
  and and_6 (and_6_out, not_11_out, not_12_out, not_13_out);
  not not_11 (not_11_out, fct_3[2]);
  not not_12 (not_12_out, fct_3[1]);
  not not_13 (not_13_out, fct_3[0]);
  and and_7 (and_7_out, opcode[6], opcode[5], not_14_out, not_15_out, not_16_out, opcode[1], opcode[0]);
  not not_14 (not_14_out, opcode[4]);
  not not_15 (not_15_out, opcode[3]);
  not not_16 (not_16_out, opcode[2]);
  and and_8 (MUX_SUB, and_7_out, and_9_out);
  or or_1 (or_1_out, and_2_out, and_5_out);
  not not_17 (not_17_out, fct_3[2]);
  Delay #(.delayTime(10)) delay_1 (.in(or_2_out), .out(W_REG));
  or or_2 (or_2_out, or_3_out, or_5_out);
  or or_3 (or_3_out, or_1_out, or_4_out);
  or or_4 (or_4_out, MUX_SUB, MUX_SORTIE);
  and and_9 (and_9_out, not_17_out, not_18_out, fct_3[0]);
  not not_18 (not_18_out, fct_3[1]);
  or or_5 (or_5_out, or_6_out, and_19_out);
  or or_6 (or_6_out, and_17_out, and_19_out);
  and and_10 (and_10_out, not_19_out, not_20_out, not_22_out, not_21_out, not_23_out, opcode[1], opcode[0]);
  not not_19 (not_19_out, opcode[6]);
  not not_20 (not_20_out, opcode[5]);
  not not_21 (not_21_out, opcode[3]);
  not not_22 (not_22_out, opcode[4]);
  or or_7 (or_7_out, or_8_out, or_10_out);
  or or_8 (or_8_out, and_2_out, MUX_SUB);
  and and_11 (MUX_SORTIE, and_10_out, and_12_out);
  not not_23 (not_23_out, opcode[2]);
  or or_9 (MUX_UAL, or_7_out, or_11_out);
  or or_10 (or_10_out, MUX_SUB, MUX_SORTIE);
  and and_12 (and_12_out, not_24_out, fct_3[1], not_25_out);
  not not_24 (not_24_out, fct_3[2]);
  or or_11 (or_11_out, or_12_out, and_17_out);
  or or_12 (or_12_out, MUX_IMM, and_17_out);
  not not_25 (not_25_out, fct_3[0]);
  or or_13 (RAM_RESULT, or_14_out, or_15_out);
  or or_14 (or_14_out, and_2_out, and_5_out);
  or or_15 (or_15_out, MUX_SUB, MUX_IMM);
  and and_13 (and_13_out, not_26_out, opcode[5], not_27_out, not_28_out, not_29_out, opcode[1], opcode[0]);
  not not_26 (not_26_out, opcode[6]);
  not not_27 (not_27_out, opcode[4]);
  and and_14 (MUX_IMM, and_13_out, and_15_out);
  not not_28 (not_28_out, opcode[3]);
  not not_29 (not_29_out, opcode[2]);
  and and_15 (and_15_out, not_30_out, fct_3[1], not_31_out);
  not not_30 (not_30_out, fct_3[2]);
  not not_31 (not_31_out, fct_3[0]);
  and and_16 (and_16_out, opcode[6], opcode[5], not_32_out, not_33_out, opcode[2], opcode[1], opcode[0]);
  not not_32 (not_32_out, opcode[4]);
  not not_33 (not_33_out, opcode[3]);
  and and_17 (and_17_out, and_16_out, and_18_out);
  and and_18 (and_18_out, not_34_out, not_35_out, not_36_out);
  not not_34 (not_34_out, fct_3[2]);
  not not_35 (not_35_out, fct_3[1]);
  not not_36 (not_36_out, fct_3[0]);
  or or_16 (MUX_PC, and_17_out, and_19_out);
  and and_19 (and_19_out, opcode[6], opcode[5], not_37_out, opcode[3], opcode[2], opcode[1], opcode[0]);
  not not_37 (not_37_out, opcode[4]);

  assign MUX_SW = MUX_IMM;
  assign OE_RAM = MUX_SORTIE;
  assign WE_RAM = MUX_IMM;

  // Notes on the sheet:
  //   ADDI
  //   ADD
  //   SUB
  //   LW
  //   SW
  //   JALR
  //   JAL
endmodule
