// Digital circuit registre8.dig as structural Verilog
module registre8 (
  input  [31:0] \reg ,
  input  W_reg,
  input  [2:0] rs1,
  input  [2:0] rs2,
  input  [2:0] rd,
  output [31:0] src1,
  output [31:0] src2
);

  wire and_1_out, and_2_out, and_3_out, and_4_out, and_5_out, and_6_out, and_7_out, and_8_out,
       decoder_1_out_0, decoder_1_out_1, decoder_1_out_2, decoder_1_out_3, decoder_1_out_4, decoder_1_out_5,
       decoder_1_out_6, decoder_1_out_7, decoder_2_out_0, decoder_2_out_1, decoder_2_out_2, decoder_2_out_3,
       decoder_2_out_4, decoder_2_out_5, decoder_2_out_6, decoder_2_out_7, decoder_3_out_0, decoder_3_out_1,
       decoder_3_out_2, decoder_3_out_3, decoder_3_out_4, decoder_3_out_5, decoder_3_out_6, decoder_3_out_7;
  wire [31:0] R0_q, R1_q, R2_q, R3_q, R4_q, R5_q, R6_q, R7_q;

  Decoder #(.Selector_Bits(3)) decoder_1 (
    .sel(rd), .out_0(decoder_1_out_0), .out_1(decoder_1_out_1), .out_2(decoder_1_out_2),
    .out_3(decoder_1_out_3), .out_4(decoder_1_out_4), .out_5(decoder_1_out_5), .out_6(decoder_1_out_6),
    .out_7(decoder_1_out_7));
  and and_1 (and_1_out, W_reg, decoder_1_out_0);
  and and_2 (and_2_out, W_reg, decoder_1_out_1);
  and and_3 (and_3_out, W_reg, decoder_1_out_2);
  and and_4 (and_4_out, W_reg, decoder_1_out_3);
  and and_5 (and_5_out, W_reg, decoder_1_out_4);
  and and_6 (and_6_out, W_reg, decoder_1_out_5);
  and and_7 (and_7_out, W_reg, decoder_1_out_6);
  and and_8 (and_8_out, W_reg, decoder_1_out_7);
  D_FF #(.Bits(32)) R0 (.D(\reg ), .C(and_1_out), .Q(R0_q));  // open: nQ
  D_FF #(.Bits(32)) R1 (.D(\reg ), .C(and_2_out), .Q(R1_q));  // open: nQ
  D_FF #(.Bits(32)) R2 (.D(\reg ), .C(and_3_out), .Q(R2_q));  // open: nQ
  D_FF #(.Bits(32)) R3 (.D(\reg ), .C(and_4_out), .Q(R3_q));  // open: nQ
  D_FF #(.Bits(32)) R4 (.D(\reg ), .C(and_5_out), .Q(R4_q));  // open: nQ
  D_FF #(.Bits(32)) R5 (.D(\reg ), .C(and_6_out), .Q(R5_q));  // open: nQ
  D_FF #(.Bits(32)) R6 (.D(\reg ), .C(and_7_out), .Q(R6_q));  // open: nQ
  D_FF #(.Bits(32)) R7 (.D(\reg ), .C(and_8_out), .Q(R7_q));  // open: nQ
  assign src1 = decoder_2_out_0 ? R0_q : 32'bz;  // Driver driver_1
  Decoder #(.Selector_Bits(3)) decoder_2 (
    .sel(rs1), .out_0(decoder_2_out_0), .out_1(decoder_2_out_1), .out_2(decoder_2_out_2),
    .out_3(decoder_2_out_3), .out_4(decoder_2_out_4), .out_5(decoder_2_out_5), .out_6(decoder_2_out_6),
    .out_7(decoder_2_out_7));
  assign src1 = decoder_2_out_1 ? R1_q : 32'bz;  // Driver driver_2
  assign src1 = decoder_2_out_2 ? R2_q : 32'bz;  // Driver driver_3
  assign src1 = decoder_2_out_3 ? R3_q : 32'bz;  // Driver driver_4
  assign src1 = decoder_2_out_4 ? R4_q : 32'bz;  // Driver driver_5
  assign src1 = decoder_2_out_5 ? R5_q : 32'bz;  // Driver driver_6
  assign src1 = decoder_2_out_6 ? R6_q : 32'bz;  // Driver driver_7
  assign src1 = decoder_2_out_7 ? R7_q : 32'bz;  // Driver driver_8
  assign src2 = decoder_3_out_0 ? R0_q : 32'bz;  // Driver driver_9
  Decoder #(.Selector_Bits(3)) decoder_3 (
    .sel(rs2), .out_0(decoder_3_out_0), .out_1(decoder_3_out_1), .out_2(decoder_3_out_2),
    .out_3(decoder_3_out_3), .out_4(decoder_3_out_4), .out_5(decoder_3_out_5), .out_6(decoder_3_out_6),
    .out_7(decoder_3_out_7));
  assign src2 = decoder_3_out_1 ? R1_q : 32'bz;  // Driver driver_10
  assign src2 = decoder_3_out_2 ? R2_q : 32'bz;  // Driver driver_11
  assign src2 = decoder_3_out_3 ? R3_q : 32'bz;  // Driver driver_12
  assign src2 = decoder_3_out_4 ? R4_q : 32'bz;  // Driver driver_13
  assign src2 = decoder_3_out_5 ? R5_q : 32'bz;  // Driver driver_14
  assign src2 = decoder_3_out_6 ? R6_q : 32'bz;  // Driver driver_15
  assign src2 = decoder_3_out_7 ? R7_q : 32'bz;  // Driver driver_16
endmodule
