// Digital circuit rv32_manuel.dig as structural Verilog
module rv32_manuel (
  input  MUX_JALR,
  input  W_PC,
  input  GATE_PC,
  input  W_RI,
  input  MUX_S,
  input  GATE_RS2,
  input  GATE_RES,
  input  MUX_SUB,
  input  MUX_UAL,
  input  W_MAR,
  input  MUX_MDR,
  input  W_MDR,
  input  OE_RAM,
  input  WE_RAM,
  input  GATE_MDR,
  input  W_REG,
  output [6:0] OPCODE
);

  wire boite_1_p_np, multiplexer_6_out, not_1_out;
  wire [0:0] and_1_out;
  wire [7:0] RI_q_2;
  wire [9:0] RI_q_4;
  wire [11:0] multiplexer_4_out;
  wire [11:7] RI_q;
  wire [20:11] RI_q_3;
  wire [31:0] add_1_s, bitextender_1_out, bitextender_2_out, bitextender_3_out, br_1_src1, br_1_src2,
       driver_1_out, driver_2_out, driver_3_out, MAR_q, MDR_q, multiplexer_1_out, multiplexer_2_out,
       multiplexer_3_out, multiplexer_5_out, pc_q, ual_1_res;

  Multiplexer #(.Selector_Bits(2), .Bits(32)) multiplexer_1 (
    .sel({OPCODE[2], and_1_out[0]}), .in_0(32'h4), .in_1(bitextender_1_out), .in_2(bitextender_2_out),
    .in_3({32{1'b0}}), .out(multiplexer_1_out));
  BitExtender #(.inputBits(13), .outputBits(32)) bitextender_1 (
    .in({RI_q_3[20], RI_q[7], RI_q_4[9:4], RI_q[11:8], 1'b0}), .out(bitextender_1_out));
  Add #(.Bits(32)) add_1 (.a(pc_q), .b(multiplexer_1_out), .c_i(1'b0), .s(add_1_s));  // open: c_o
  and and_1 (and_1_out[0], boite_1_p_np, ~OPCODE[2]);  // And
  Multiplexer #(.Bits(32)) multiplexer_2 (.sel(MUX_JALR), .in_0(add_1_s), .in_1(driver_2_out), .out(multiplexer_2_out));
  boite boite_1 (.fct3(RI_q_2[2:0]), .res(driver_1_out), .p_np(boite_1_p_np));
  BitExtender #(.inputBits(21), .outputBits(32)) bitextender_2 (
    .in({RI_q_3[20], RI_q_2, RI_q_3[11], RI_q_4, 1'b0}), .out(bitextender_2_out));
  assign driver_1_out = OPCODE[6] ? ual_1_res : 32'bz;  // Driver driver_1
  D_FF #(.Bits(32)) pc (.D(multiplexer_2_out), .C(W_PC), .Q(pc_q));  // open: nQ
  assign driver_2_out = GATE_PC ? pc_q : 32'bz;  // Driver driver_2
  D_FF #(.Bits(32)) MAR (.D(driver_2_out), .C(W_MAR), .Q(MAR_q));  // open: nQ
  D_FF #(.Bits(32)) RI (
    .D(driver_2_out), .C(W_RI), .Q({RI_q_3[20], RI_q_4, RI_q_3[11], RI_q_2, RI_q, OPCODE}));  // open: nQ
  Multiplexer #(.Bits(32)) multiplexer_3 (
    .sel(MUX_MDR), .in_0(driver_2_out), .in_1(driver_3_out), .out(multiplexer_3_out));
  Multiplexer #(.Bits(12)) multiplexer_4 (
    .sel(MUX_S), .in_0({RI_q_3[20], RI_q_4, RI_q_3[11]}), .in_1({RI_q_3[20], RI_q_4[9:4], RI_q}),
    .out(multiplexer_4_out));
  assign driver_3_out = OE_RAM ? MDR_q : 32'bz;  // Driver driver_3
  D_FF #(.Bits(32)) MDR (.D(multiplexer_3_out), .C(W_MDR), .Q(MDR_q));  // open: nQ
  BitExtender #(.inputBits(12), .outputBits(32)) bitextender_3 (.in(multiplexer_4_out), .out(bitextender_3_out));
  BR br_1 (
    .res(ual_1_res), .rd(RI_q), .rs1(RI_q_2[7:3]), .rs2({RI_q_4[3:0], RI_q_3[11]}), .W_reg(W_REG),
    .src1(br_1_src1), .src2(br_1_src2));
  assign driver_2_out = GATE_MDR ? MDR_q : 32'bz;  // Driver driver_4
  not not_1 (not_1_out, OE_RAM);
  Multiplexer #(.Bits(32)) multiplexer_5 (
    .sel(MUX_UAL), .in_0(br_1_src2), .in_1(bitextender_3_out), .out(multiplexer_5_out));
  assign driver_2_out = GATE_RS2 ? br_1_src2 : 32'bz;  // Driver driver_5
  Multiplexer multiplexer_6 (.sel(MUX_SUB), .in_0(RI_q_4[9]), .in_1(1'b1), .out(multiplexer_6_out));
  RAMSinglePortSel #(.AddrBits(8), .isProgramMemory("true"), .Bits(32)) ramsingleportsel_1 (
    .A(MAR_q[9:2]), .CS(1'b1), .WE(WE_RAM), .OE(not_1_out), .D(driver_3_out));
  ual ual_1 (
    .src1(br_1_src1), .sub(multiplexer_6_out), .src2(multiplexer_5_out), .fct3(RI_q_2[2:0]), .res(ual_1_res));  // open: cout
  assign driver_2_out = GATE_RES ? ual_1_res : 32'bz;  // Driver driver_6
endmodule
