// Digital circuit rv32pipeliné.dig as structural Verilog
module \rv32pipeliné  (
  input  IF_ID,
  input  ID_EX,
  input  muxjalr,
  input  EX_MEX,
  input  in_6,
  input  W_PC,
  output [31:0] out_5
);

  wire boite_1_p_np, multiplexer_5_out, MUX_IMM, MUX_S, MUX_SORTIE, MUX_SUB, MUX_UAL, OE_RAM, RAM_RESULT,
       W_reg, WE_RAM, WREG_synchro;
  wire [0:0] and_1_out;
  wire [2:0] fct3;
  wire [5:0] EX_MEM2_q, IF_ID_q_3, MEM_WB2_q;
  wire [6:0] Opcode;
  wire [7:0] bitextender_4_out, multiplexer_7_out;
  wire [11:0] multiplexer_3_out;
  wire [12:1] IF_ID_q;
  wire [19:1] IF_ID_q_2;
  wire [31:0] add_1_s, bitextender_1_out, bitextender_2_out, bitextender_3_out, br_1_src1, br_1_src2,
       driver_1_out, driver_2_out, MEM_WB1_q, multiplexer_1_out, multiplexer_2_out, multiplexer_4_out,
       multiplexer_6_out, multiplexer_8_out, pc_q, ramsingleportsel_1_d, ROM_d, ual_1_res;
  wire [63:0] EX_MEM1_q, ID_EX1_q, ID_EX2_q;
  wire [63:32] IF_ID_q_4;

  Multiplexer #(.Selector_Bits(2), .Bits(32)) multiplexer_1 (
    .sel({Opcode[2], and_1_out[0]}), .in_0(32'h4), .in_1(bitextender_1_out), .in_2(bitextender_2_out),
    .in_3({32{1'b0}}), .out(multiplexer_1_out));
  Add #(.Bits(32)) add_1 (.a(pc_q), .b(multiplexer_1_out), .c_i(1'b0), .s(add_1_s));  // open: c_o
  Multiplexer #(.Bits(32)) multiplexer_2 (
    .sel(muxjalr), .in_0(add_1_s), .in_1(ID_EX1_q[31:0]), .out(multiplexer_2_out));
  and and_1 (and_1_out[0], boite_1_p_np, ~Opcode[2]);  // And
  BitExtender #(.inputBits(13), .outputBits(32)) bitextender_1 (
    .in({IF_ID_q[12:11], IF_ID_q_3, IF_ID_q[4:1], 1'b0}), .out(bitextender_1_out));
  D_FF #(.Bits(32)) pc (.D(multiplexer_2_out), .C(W_PC), .Q(pc_q));  // open: nQ
  assign driver_1_out = Opcode[6] ? MEM_WB1_q : 32'bz;  // Driver driver_1
  boite boite_1 (.fct3(fct3), .res(driver_1_out), .p_np(boite_1_p_np));
  BitExtender #(.inputBits(21), .outputBits(32)) bitextender_2 (
    .in({IF_ID_q[12], IF_ID_q_2[19:15], fct3, IF_ID_q_2[11], IF_ID_q_3, IF_ID_q_2[4:1], 1'b0}),
    .out(bitextender_2_out));
  ROM #(.AddrBits(24), .isProgramMemory("true"), .Bits(32)) ROM (.A(pc_q[23:0]), .sel(1'b1), .D(ROM_d));
  Add #(.Bits(32)) add_2 (.a(pc_q), .b(32'h4), .c_i(1'b0), .s(out_5));  // open: c_o
  D_FF #(.Bits(64)) u_IF_ID (
    .D({out_5, ROM_d}), .C(IF_ID),
    .Q({IF_ID_q_4, IF_ID_q[12], IF_ID_q_3, IF_ID_q_2[4:1], IF_ID_q_2[11], IF_ID_q_2[19:15], fct3, IF_ID_q[4:1], IF_ID_q[11], Opcode}));  // open: nQ
  BR br_1 (
    .res(MEM_WB1_q), .rd(MEM_WB2_q[4:0]), .rs1(IF_ID_q_2[19:15]), .rs2({IF_ID_q_2[4:1], IF_ID_q_2[11]}),
    .W_reg(WREG_synchro), .src1(br_1_src1), .src2(br_1_src2));
  Multiplexer #(.Bits(12)) multiplexer_3 (
    .sel(MUX_IMM), .in_0({IF_ID_q[12], IF_ID_q_3, IF_ID_q_2[4:1], IF_ID_q_2[11]}),
    .in_1({IF_ID_q[12], IF_ID_q_3, IF_ID_q[4:1], IF_ID_q[11]}), .out(multiplexer_3_out));
  BitExtender #(.inputBits(12), .outputBits(32)) bitextender_3 (.in(multiplexer_3_out), .out(bitextender_3_out));
  D_FF #(.Bits(64)) ID_EX1 (.D({br_1_src2, br_1_src1}), .C(ID_EX), .Q(ID_EX1_q));  // open: nQ
  D_FF #(.Bits(64)) ID_EX2 (
    .D({{26{1'b0}}, WREG_synchro, IF_ID_q[4:1], IF_ID_q[11], bitextender_3_out}), .C(ID_EX), .Q(ID_EX2_q));  // open: nQ
  Multiplexer #(.Bits(32)) multiplexer_4 (
    .sel(MUX_UAL), .in_0(ID_EX1_q[63:32]), .in_1(ID_EX2_q[31:0]), .out(multiplexer_4_out));
  Multiplexer multiplexer_5 (.sel(MUX_SUB), .in_0(IF_ID_q_3[5]), .in_1(1'b1), .out(multiplexer_5_out));
  ual ual_1 (
    .src1(ID_EX1_q[31:0]), .sub(multiplexer_5_out), .src2(multiplexer_4_out), .fct3(fct3), .res(ual_1_res));  // open: cout
  D_FF #(.Bits(64)) EX_MEM1 (.D({ID_EX1_q[63:32], ual_1_res}), .C(EX_MEX), .Q(EX_MEM1_q));  // open: nQ
  D_FF #(.Bits(6)) EX_MEM2 (.D(ID_EX2_q[37:32]), .C(EX_MEX), .Q(EX_MEM2_q));  // open: nQ
  Multiplexer #(.Bits(32)) multiplexer_6 (
    .sel(MUX_S), .in_0(EX_MEM1_q[31:0]), .in_1(EX_MEM1_q[63:32]), .out(multiplexer_6_out));
  BitExtender #(.inputBits(6), .outputBits(8)) bitextender_4 (.in(EX_MEM2_q), .out(bitextender_4_out));
  and and_2 (WREG_synchro, in_6, W_reg);
  Multiplexer #(.Bits(8)) multiplexer_7 (
    .sel(MUX_S), .in_0(bitextender_4_out), .in_1(EX_MEM1_q[7:0]), .out(multiplexer_7_out));
  RAMSinglePortSel #(.AddrBits(8), .isProgramMemory("true"), .Bits(32)) ramsingleportsel_1 (
    .A(multiplexer_7_out), .CS(1'b1), .WE(WE_RAM), .OE(OE_RAM), .D(ramsingleportsel_1_d));
  assign driver_2_out = OE_RAM ? EX_MEM1_q[31:0] : 32'bz;  // Driver driver_2
  circuitdecontrolerv32pipeline circuitdecontrolerv32pipeline_1 (
    .opcode(Opcode), .fct_3(fct3), .W_REG(W_reg), .MUX_UAL(MUX_UAL), .MUX_SORTIE(MUX_SORTIE),
    .MUX_SUB(MUX_SUB), .OE_RAM(OE_RAM), .RAM_RESULT(RAM_RESULT), .WE_RAM(WE_RAM), .MUX_IMM(MUX_IMM),
    .MUX_SW(MUX_S));  // open: MUX_PC
  assign ramsingleportsel_1_d = RAM_RESULT ? multiplexer_6_out : 32'bz;  // Driver driver_3
  D_FF #(.Bits(6)) MEM_WB2 (.D(EX_MEM2_q), .C(in_6), .Q(MEM_WB2_q));  // open: nQ
  Multiplexer #(.Bits(32)) multiplexer_8 (
    .sel(MUX_SORTIE), .in_0(ramsingleportsel_1_d), .in_1(driver_2_out), .out(multiplexer_8_out));
  D_FF #(.Bits(32)) MEM_WB1 (.D(multiplexer_8_out), .C(in_6), .Q(MEM_WB1_q));  // open: nQ

  // Other names for the same wires on the sheet: EX_MEM = EX_MEX; MEM_WB = in_6
endmodule
